# Fritzing sketch Relay Module (saved by Fritzing 0.9.3b)
circuit board: 9.42151cm x 9.65502cm
breadboards: 3

parts:
  IC1 = MCP23017 I2C I/O Expander
  J1 = male pin header, 3 pins [form="♂ (male)"]
  J2 = male pin header, 3 pins [form="♂ (male)"]
  J3 = male pin header, 3 pins [form="♂ (male)"]
  C1 = Ceramic Capacitor [capacitance=0.1mF package="100 mil [THT, multilayer]"]
  R1 = Resistor [tolerance=±5% resistance=150 package=THT]
  LED1 = LED - 5mm [color="Green (565nm)" package="5 mm [THT]"]
  C2 = Ceramic Capacitor [capacitance=0.1mF package="100 mil [THT, multilayer]"]
  R2 = Resistor [tolerance=±5% resistance=4.7k package=THT]
  R3 = Resistor [tolerance=±5% resistance=4.7k package=THT]
  D1 = Rectifier Diode [part_number=1N4001 package="300 mil [THT]"]
  R4 = Resistor [tolerance=±5% resistance=4.7k package=THT]
  REL1 = RELAY [package=relay-jzc]
  REL2 = RELAY [package=relay-jzc]
  REL3 = RELAY [package=relay-jzc]
  REL4 = RELAY [package=relay-jzc]
  REL5 = RELAY [package=relay-jzc]
  J5 = screw terminal, 3 pins
  J6 = screw terminal, 3 pins
  J7 = screw terminal, 3 pins
  J8 = screw terminal, 3 pins
  J9 = screw terminal, 3 pins
  IC2 = ULN2803A [package=THT]
  LED2 = LED - 3mm [color="Green (570nm)" package="3 mm [THT]"]
  LED3 = LED - 3mm [color="Green (570nm)" package="3 mm [THT]"]
  LED4 = LED - 3mm [color="Green (570nm)" package="3 mm [THT]"]
  LED5 = LED - 3mm [color="Green (570nm)" package="3 mm [THT]"]
  LED6 = LED - 3mm [color="Green (570nm)" package="3 mm [THT]"]
  J4 = screw terminal, 5 pins

nets:
  N1: IC1.GPB0, IC2.In_1
  N2: IC1.GPB1, IC2.In_2
  N3: IC1.GPB2, IC2.In_3
  N4: IC1.GPB3, IC2.In_4
  N5: IC1.GPB4, IC2.In_5
  N6: IC1.GPB5, IC1.GPA2
  N7: IC1.VDD, C1.0, R4.Pin_0, J4.pin5
  N8: IC1.VSS, J1.pin1, J2.pin1, J3.pin1, C1.1, R1.Pin_0, C2.1, REL1.COIL2, REL2.COIL2, REL3.COIL2, REL4.COIL2, REL5.COIL2, IC2.0V, LED2.cathode, LED3.cathode, LED4.cathode, LED5.cathode, LED6.cathode, J4.pin4
  N9: IC1.SCL, R2.Pin_0, J4.pin2
  N10: IC1.SDA, R3.Pin_0, J4.pin1
  N11: IC1.A0, J1.pin2
  N12: IC1.A1, J2.pin2
  N13: IC1.A2, J3.pin2
  N14: IC1.RESET, R4.Pin_1
  N15: IC1.GPA3, LED6.anode
  N16: IC1.GPA4, LED5.anode
  N17: IC1.GPA5, LED4.anode
  N18: IC1.GPA6, LED3.anode
  N19: IC1.GPA7, LED2.anode
  N20: J1.pin3, J2.pin3, J3.pin3, D1.cathode
  N21: R1.Pin_1, LED1.cathode
  N22: LED1.anode, C2.0, R2.Pin_1, R3.Pin_1, D1.anode, IC2.COM_-_Common, J4.pin3
  N23: REL1.NC, J5.pin3
  N24: REL1.NO, J5.pin1
  N25: REL1.MAIN, J5.pin2
  N26: REL1.COIL1, IC2.Out_1
  N27: REL2.NC, J6.pin3
  N28: REL2.NO, J6.pin1
  N29: REL2.MAIN, J6.pin2
  N30: REL2.COIL1, IC2.Out_2
  N31: REL3.NC, J7.pin3
  N32: REL3.NO, J7.pin1
  N33: REL3.MAIN, J7.pin2
  N34: REL3.COIL1, IC2.Out_3
  N35: REL4.NC, J8.pin3
  N36: REL4.NO, J8.pin1
  N37: REL4.MAIN, J8.pin2
  N38: REL4.COIL1, IC2.Out_4
  N39: REL5.NC, J9.pin3
  N40: REL5.NO, J9.pin1
  N41: REL5.MAIN, J9.pin2
  N42: REL5.COIL1, IC2.Out_5

notes:
  PWR
  MCP23017
  ULN2803A
  RELAY 1
  Relay 2
  Relay 3
  Relay 4
  Relay 5
  C
  A0
  +
  -
  A1
  A2
  Address Selection
  SCL
  SDA
  NC
  NO
  CyGate4 - Relay Module Rev 1.2
  CyGate4 - Relay Module, Relay Module for CyGate4, 1.2
  Copyright (c) 2021 Cyrus Brunner
  www.cyrusbuilt.net
  FAB 001002 ASSY 001002
  Address Select
  RST
  GND
  +5V

custom parts:
  MCP23017 I2C I/O Expander: The MCP23017 uses two i2c pins (these can be shared with other i2c devices), and in exchange gives you 16 general purpose pins. You can set each of 16 pins to be input, output, input with a pullup or open drain. There's even the ability to get an interrupt via an external pin when any of the inputs change so you don't have to keep polling the chip.
